# Fritzing sketch hydroponics_schematic (saved by Fritzing 0.9.3b)
breadboards: 2

parts:
  Part2 = Adafruit AS7341
  DHT1 = DHT22 Humidity and Temperature Sensor
  Part3 = Arduino Uno (Rev3)
  KY-1 = Relay [package=THT]
  KY-2 = Relay [package=THT]
  KY-3 = Relay [package=THT]
  F1 = Fan - Ventilador [package=THT]
  S2 = PH meter [package=THT]  # not connected
  U1 = Vibration Motor- ROB-08449 [package=vibe-motor-10mm]  # not connected
  hc-sr1 = hc-sr04
  Part4 = Soil Moisture Sensor  # not connected
  M1 = DC Motor
  KY-4 = Relay [package=THT]
  Raspberry_Pi_1 = Raspberry Pi 3 [part_number=RPI-3-V1.2]  # not connected
  Power_plug2 = Power plug
  LED1 = LEDs [package=led10mm]
  DS1 = DS18B20 1-Wire Temperature Sensor [part_number=DS18B20]
  Power_plug3 = Power plug  # not connected
  Power_plug4 = Power plug  # not connected
  Power_plug5 = Power plug
  M2 = DC Motor

nets:
  N1: Part2.SDA, Part3.A4/SDA
  VCC: Part2.VCC, DHT1.VDD, Part3.5V, KY-1.power, KY-2.power, KY-3.power, hc-sr1.VCC
  GND: Part2.GND, Part3.GND, KY-1.ground, KY-2.ground, hc-sr1.GND, KY-4.ground, DS1.GND
  N2: Part2.SCL, Part3.A5/SCL
  N3: DHT1.DATA, Part3.D4
  N4: DHT1.GND, KY-3.ground
  N5: Part3.D8, hc-sr1.Echo
  N6: Part3.D9_PWM, hc-sr1.Trig
  N7: Part3.D10_PWM/SS, KY-1.in
  N8: Part3.D11_PWM/MOSI, KY-2.in
  N9: Part3.D12/MISO, KY-3.in
  N10: Part3.D13/SCK, KY-4.in
  N11: Part3.D7, DS1.DQ
  N12: KY-1.NO, F1.5V
  N13: KY-2.NO, LED1.C
  N14: KY-3.COM, KY-4.COM, Power_plug2.VCC
  N15: KY-3.NO, M2.pin_2
  GND_2: F1.GND, M1.pin_1, Power_plug2.GND, M2.pin_1
  N16: M1.pin_2, KY-4.NO
  N17: KY-4.power, DS1.VDD
  N18: LED1.A, Power_plug5.GND

notes:
  pH Meter PH-4502C
  V-----------
  GND------
  GND
  Po---------
  Do
  To
  Water atomizer
  Digital (Yellow)
  5V (Red)
  GND (Black)
  Grow lights 5V
  TDS sensor
  GND
  VCC
  A
  DHT22 temperature & humidity
  Fan 5V
  Water pump
  (immersed in water)
  Air pump
  (air stone connected to it)
  Color sensor AS7341
  Ultrasonic distance sensor
  5V power supply for actuators
  DS18B20 waterproof temperature sensor
  RPi power supply
  Arduino power supply
  Serial communication
  Arduino <-> RPi
  5V power supply for lights

custom parts:
  Relay: The Keyes 5V relay module is suitable for SCM development, home appliance control. It uses a 5V~12V TIL control signal which can control DC / AC signal.
  Fan - Ventilador: Ventilador de 2 pines, se encuentra comunmente en computadoras de escritorio
